# Fritzing sketch CircuitPlayground (saved by Fritzing 0.9.3b)

parts:
  Part1 = Adafruit Circuit Playground Dev Edition [part_number="Adafruit #3000"]
  BAT1 = Battery Holders [package=lipo-1100mAh]  # not connected
  NEOPIXEL3 = Neopixel Strip -- White (30/m)
  C1 = Capacitor Polarized [package=cpol-radial-100uf-25v]
  R1 = Resistor [tolerance=±5% resistance=220 package=THT]

nets:
  N1: Part1.D6, R1.Pin_0
  GND: Part1.GND, NEOPIXEL3.GND, C1.-
  N2: Part1.VBAT, NEOPIXEL3.+5V, C1.+
  N3: NEOPIXEL3.Din, R1.Pin_1

notes:
  300-500 Ohm
  1000 uF, notice the polarity

custom parts:
  Adafruit Circuit Playground Dev Edition: Would you like to learn electronics, with an all-in-one board that has sensors and LEDs built in? Circuit Playground is here - and it's the best way to practice programming on real hardware with no soldering or sewing required! Circuit Playground features an ATmega32u4 processor, just like our popular Flora. The board's also round and has alligator-clip pads around it so you don't have to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
  Neopixel Strip -- White (30/m): These NeoPixel strips have 30 digitally-addressable pixel LEDs per meter and are very affordable and are only 12.5 mm wide, 10 mm if you remove the strip from the casing.
